# Fritzing sketch SN74HC165N (saved by Fritzing 0.7.10b)
breadboards: 1

parts:
  Arduino1 = Arduino
  S3 = Pushbutton [package=THT]
  S6 = Pushbutton [package=THT]
  R1 = Resistor [tolerance=±5% resistance=10k package=THT]
  S4 = Pushbutton [package=THT]
  U1 = 74HC165 [part_number=SN74LS165 package="DIP16 [THT]"]
  S8 = Pushbutton [package=THT]
  R5 = Resistor [tolerance=±5% resistance=10k package=THT]
  R8 = Resistor [tolerance=±5% resistance=10k package=THT]
  S5 = Pushbutton [package=THT]
  S7 = Pushbutton [package=THT]
  S2 = Pushbutton [package=THT]
  R9 = Resistor [tolerance=±5% resistance=10k package=THT]
  S9 = Pushbutton [package=THT]
  R10 = Resistor [tolerance=±5% resistance=10k package=THT]
  R12 = Resistor [tolerance=±5% resistance=10k package=THT]
  R13 = Resistor [tolerance=±5% resistance=10k package=THT]
  R14 = Resistor [tolerance=±5% resistance=10k package=THT]

nets (from the breadboard view):
  GND: Arduino1.GND, U1.GND, U1.MR, U1.Q0
  N1: Arduino1.D9, U1.Q7'
  N2: Arduino1.D8, U1.Q1
  N3: Arduino1.D7, U1.Q2
  +5V: Arduino1.+5V, S3.leg0, S6.leg0, R1.Pin_0, S4.leg0, U1.VCC, S8.leg0, R5.Pin_0, R8.Pin_0, S5.leg0, S7.leg0, S2.leg0, R9.Pin_0, S9.leg0, R10.Pin_0, R12.Pin_0, R13.Pin_0, R14.Pin_0
  N4: S3.leg1, U1.Q6, R13.Pin_1
  N5: S6.leg1, U1.ST_CP, R10.Pin_1
  N6: R1.Pin_1, U1.DS, S7.leg1
  N7: S4.leg1, U1.Q3, R9.Pin_1
  N8: U1.Q4, R5.Pin_1, S5.leg1
  N9: U1.Q5, S2.leg1, R12.Pin_1
  N10: U1.SH_CP, R8.Pin_1, S9.leg1
  N11: U1.OE, S8.leg1, R14.Pin_1

custom parts:
  74HC165: 8-bit parallel-load shift registers
